// Digital circuit processador8Bits.dig as structural Verilog
module processador8Bits (
  input  [7:0] dado_a_ser_armazenado,
  input  \_1___dado_é_armazenado ,
  input  [2:0] seleciona_registrador,
  input  in_4,
  input  [2:0] in_5,
  input  [2:0] in_6,
  input  [3:0] \endereço_onde_pegar___armazenar ,
  input  [7:0] dado_a_ser_armazenado_2,
  input  _1___dado_armazenado_no_clock,
  input  in_13,
  input  in_14,
  input  [1:0] in_15,
  output [7:0] out_7,
  output [7:0] out_8,
  output [7:0] out_9
);

  wire [7:0] memoria_d, multiplexer_1_out, u_BR_CONTROLLER_ram, u_BR_CONTROLLER_ula_a, u_BR_CONTROLLER_ula_b,
       u_ULA_s;

  Multiplexer #(.Bits(8)) multiplexer_1 (.in_0(memoria_d), .in_1(u_ULA_s), .out(multiplexer_1_out));  // open: sel
  RegisterFile #(.AddrBits(3), .Bits(8)) BANCO ();  // open: Din, we, Rw, C, Ra, Rb, Da, Db
  BR_CONTROLLER #(.applicationType("GHDL")) u_BR_CONTROLLER (
    .VALUE_IN(multiplexer_1_out), .OP(in_15), .RAM(u_BR_CONTROLLER_ram), .ULA_A(u_BR_CONTROLLER_ula_a),
    .ULA_B(u_BR_CONTROLLER_ula_b));
  RegisterFile #(.AddrBits(3), .Bits(8)) BANCO_2 (
    .Din(dado_a_ser_armazenado), .we(\_1___dado_é_armazenado ), .Rw(seleciona_registrador), .C(in_4),
    .Ra(in_5), .Rb(in_6), .Da(out_7), .Db(out_8));
  RAMDualPort #(.AddrBits(4), .isProgramMemory("true"), .Bits(8)) memoria (
    .Din(u_BR_CONTROLLER_ram), .D(memoria_d));  // open: A, str, C, ld
  ULA #(.applicationType("GHDL")) u_ULA (
    .A(u_BR_CONTROLLER_ula_a), .B(u_BR_CONTROLLER_ula_b), .S(u_ULA_s));  // open: OP
  RAMDualPort #(.AddrBits(4), .Bits(8)) ramdualport_1 (
    .A(\endereço_onde_pegar___armazenar ), .Din(dado_a_ser_armazenado_2),
    .str(_1___dado_armazenado_no_clock), .C(in_13), .ld(in_14), .D(out_9));
  // Pins of 1 and 2 bits meet at in_15
endmodule

/* Code of BR_CONTROLLER:
library IEEE;
use IEEE.std_logic_1164.all;

entity ULA is 
    port(
        VALUE_IN : in std_logic_vector(7 downto 0);
	OP : in std_logic_vector(1 downto 0); -- 0 - gravar no banco / 1 - selecionar no banco
        RAM, ULA_A, ULA_B : out std_logic_vector(7 downto 0)

    );
end ULA; 

architecture behav_ULA of ULA is
begin
    RAM <=  VALUE_IN and VALUE_IN;
end behav_ULA;
*/

/* Code of ULA:
library IEEE;
use IEEE.std_logic_1164.all;

entity ULA is 
    port(
        A, B        :   in std_logic_vector(7 downto 0);
	OP	    :   in std_logic_vector(2 downto 0);
        S           :   out std_logic_vector(7 downto 0)

    );
end ULA; 

architecture behav_ULA of ULA is
begin
    S <=  A and B;
end behav_ULA;
*/
